// Logisim project MIPS-CPU.circ as structural Verilog: 7 circuits, main circuit 多周期MIPS
module MIPS_Regifile (
  input  [31:0] Din,
  input  Clk,
  input  WE,
  input  [4:0] R1_num,
  input  [4:0] W_num,
  input  [4:0] R2_num,
  output [31:0] R1,
  output [31:0] R2
);

  // RegisterFile registerfile_1: pin names not known; wires that end beside it: Din, Clk, WE, W_num, R1_num, R2_num, R1, R2
endmodule

module ALU (
  input  [3:0] in_1,
  input  [31:0] in_2,
  input  [31:0] in_3,
  output EQ,
  output [31:0] out_5
);

  wire comparator_1_lt, comparator_2_lt;
  wire [31:0] adder_1_out, and_1_out, bit_extender_1_out, bit_extender_2_out, multiplier_1_out, not_1_out,
       or_1_out, shifter_1_out, shifter_2_out, shifter_3_out, subtractor_1_out, xor_1_out;

  // Probe on in_2
  // Probe on in_3
  Adder #(.width(32)) adder_1 (.a(in_2), .b(in_3), .out(adder_1_out));  // open: cin, cout
  Subtractor #(.width(32)) subtractor_1 (.a(in_2), .b(in_3), .out(subtractor_1_out));  // open: bin, bout
  Multiplier #(.width(32)) multiplier_1 (.a(in_2), .b(in_3), .out(multiplier_1_out));  // open: cin, cout
  Shifter #(.width(32)) shifter_1 (.in(in_2), .\dist (in_3[4:0]), .out(shifter_1_out));
  Shifter #(.width(32), .shift("lr")) shifter_2 (.in(in_2), .\dist (in_3[4:0]), .out(shifter_2_out));
  Shifter #(.width(32), .shift("ar")) shifter_3 (.in(in_2), .\dist (in_3[4:0]), .out(shifter_3_out));
  Comparator #(.width(32)) comparator_1 (.a(in_2), .b(in_3), .lt(comparator_1_lt));  // open: gt, eq
  Comparator #(.width(32), .mode("unsigned")) comparator_2 (.a(in_2), .b(in_3), .lt(comparator_2_lt));  // open: gt, eq
  assign and_1_out = in_2 & in_3;  // AND_Gate and_1, 32 bits wide
  assign or_1_out = in_2 | in_3;  // OR_Gate or_1, 32 bits wide
  assign xor_1_out = in_2 ^ in_3;  // XOR_Gate xor_1, 32 bits wide
  assign not_1_out = ~or_1_out;  // NOT_Gate not_1, 32 bits wide
  assign bit_extender_1_out = {{31{1'b0}}, comparator_1_lt};  // Bit_Extender bit_extender_1
  assign bit_extender_2_out = {{31{1'b0}}, comparator_2_lt};  // Bit_Extender bit_extender_2
  Comparator #(.width(32)) comparator_3 (.a(in_2), .b(in_3), .eq(EQ));  // open: gt, lt
  // Probe on out_5
  Multiplexer #(.select(4), .width(32)) multiplexer_1 (
    .in0(and_1_out), .in1(or_1_out), .in2(xor_1_out), .in3(adder_1_out), .in4(subtractor_1_out),
    .in5(multiplier_1_out), .in6(shifter_1_out), .in7(shifter_2_out), .in8(shifter_3_out), .in9(not_1_out),
    .in10(bit_extender_1_out), .in11(bit_extender_2_out), .out(out_5), .sel(in_1));  // open: in12, in13, in14, in15, en

  // Other names for the same wires on the sheet: A[31:0] = in_2; ALUI[3:0] = in_1; B[31:0] = in_3
endmodule

module ALUFUNC (
  input  f5,
  input  f4,
  input  f3,
  input  f2,
  input  f1,
  input  f0,
  output s3,
  output s2,
  output s1,
  output s0
);

  wire and_1_out, and_2_out, and_3_out, and_4_out, and_5_out, and_6_out, and_7_out, and_8_out, and_9_out,
       and_10_out, and_11_out, and_12_out, and_13_out, and_14_out, not_1_out, not_2_out, not_3_out,
       not_4_out, not_5_out, not_6_out, not_7_out, not_8_out, not_9_out, not_10_out, not_11_out, not_12_out,
       not_13_out, not_14_out, not_15_out, not_16_out, not_17_out, not_18_out, not_19_out, not_20_out,
       not_21_out, not_22_out, not_23_out, not_24_out, not_25_out, not_26_out, not_27_out, not_28_out,
       not_29_out;

  and and_1 (and_1_out, f1, f0);
  not not_1 (not_1_out, f5);
  not not_2 (not_2_out, f0);
  not not_3 (not_3_out, f2);
  not not_4 (not_4_out, f1);
  not not_5 (not_5_out, f4);
  not not_6 (not_6_out, f3);
  not not_7 (not_7_out, f2);
  not not_8 (not_8_out, f0);
  not not_9 (not_9_out, f5);
  not not_10 (not_10_out, f1);
  not not_11 (not_11_out, f5);
  not not_12 (not_12_out, f0);
  not not_13 (not_13_out, f2);
  not not_14 (not_14_out, f1);
  not not_15 (not_15_out, f0);
  not not_16 (not_16_out, f0);
  not not_17 (not_17_out, f2);
  not not_18 (not_18_out, f0);
  not not_19 (not_19_out, f5);
  not not_20 (not_20_out, f0);
  not not_21 (not_21_out, f3);
  not not_22 (not_22_out, f2);
  not not_23 (not_23_out, f1);
  not not_24 (not_24_out, f0);
  not not_25 (not_25_out, f4);
  not not_26 (not_26_out, f3);
  not not_27 (not_27_out, f3);
  not not_28 (not_28_out, f2);
  not not_29 (not_29_out, f0);
  or or_1 (s3, and_1_out, f3);
  and and_2 (and_2_out, not_1_out, not_2_out);
  and and_3 (and_3_out, not_3_out, not_4_out, f0);
  and and_4 (and_4_out, not_5_out, not_6_out, not_7_out, f1, not_8_out);
  and and_5 (and_5_out, not_9_out, not_10_out);
  and and_6 (and_6_out, not_11_out, not_12_out);
  and and_7 (and_7_out, not_13_out, not_14_out, not_15_out);
  and and_8 (and_8_out, f2, f1, not_16_out);
  and and_9 (and_9_out, f4, not_17_out, not_18_out);
  and and_10 (and_10_out, not_19_out, f1, not_20_out);
  and and_11 (and_11_out, f5, not_21_out, not_22_out, not_23_out, not_24_out);
  and and_12 (and_12_out, f5, f1, f0);
  and and_13 (and_13_out, f5, not_25_out, not_26_out, f2, f0);
  and and_14 (and_14_out, f5, f4, not_27_out, not_28_out, not_29_out);
  or or_2 (s2, and_2_out, and_3_out, and_4_out);
  or or_3 (s1, and_5_out, and_6_out, and_7_out, and_8_out, f3, and_9_out);
  or or_4 (s0, and_10_out, and_11_out, and_12_out, and_13_out, and_14_out);
endmodule

module ALUOP (
  input  op5,
  input  op4,
  input  op3,
  input  op2,
  input  op1,
  input  op0,
  output s3,
  output s2,
  output s1,
  output s0
);

  wire and_1_out, and_2_out, and_3_out, and_4_out, and_5_out, and_6_out, and_7_out, and_8_out, and_9_out,
       and_10_out, and_11_out, and_12_out, and_13_out, and_14_out, not_1_out, not_2_out, not_3_out,
       not_4_out, not_5_out, not_6_out, not_7_out, not_8_out, not_9_out, not_10_out, not_11_out;

  not not_1 (not_1_out, op5);
  not not_2 (not_2_out, op2);
  not not_3 (not_3_out, op2);
  not not_4 (not_4_out, op0);
  not not_5 (not_5_out, op2);
  not not_6 (not_6_out, op1);
  not not_7 (not_7_out, op1);
  and and_1 (and_1_out, op2, op1, op0);
  and and_2 (and_2_out, op4, op2, op0);
  and and_3 (and_3_out, op5, op2, op0);
  not not_8 (not_8_out, op0);
  not not_9 (not_9_out, op2);
  not not_10 (not_10_out, op1);
  and and_4 (and_4_out, not_1_out, not_2_out, op1);
  and and_5 (and_5_out, not_3_out, op1, not_4_out);
  and and_6 (and_6_out, op4, not_5_out, op1);
  and and_7 (and_7_out, op4, op2, not_6_out, op0);
  and and_8 (and_8_out, op5, op2, not_7_out, op0);
  or or_1 (s2, and_1_out, and_2_out, and_3_out);
  not not_11 (not_11_out, op2);
  and and_9 (and_9_out, op1, not_8_out);
  and and_10 (and_10_out, not_9_out, not_10_out);
  and and_11 (and_11_out, op1, op0);
  and and_12 (and_12_out, op3, op0);
  and and_13 (and_13_out, op4, op0);
  and and_14 (and_14_out, op5, op0);
  or or_2 (s3, and_4_out, and_5_out, and_6_out, and_7_out, and_8_out);
  or or_3 (s1, not_11_out, and_9_out);
  or or_4 (s0, and_10_out, and_11_out, and_12_out, and_13_out, and_14_out);
endmodule

module \多周期MIPS  (
);

  wire AluSrcA, and_1_out, and_2_out, Beq, Bne, CLK, EQ, IorD, IRWrite, JAL, JMP, JR, MemRead, MemToReg,
       MemWrite, not_1_out, PCin, PcSrc, PCWrite, RegDes, RegWrite, RST, Shamt;
  wire [1:0] AluSrcB;
  wire [3:0] AluOp;
  wire [4:0] multiplexer_3_out, multiplexer_6_out, \多周期控制器_1_out_5 ;
  wire [5:0] FUNC, OP;
  wire [9:0] multiplexer_1_out;
  wire [25:6] IR_q;
  wire [31:0] A_q, alu_1_out_5, B_q, bit_extender_1_out, bit_extender_2_out, bit_extender_3_out, C_q, DR_q,
       mips_ram_1_p2, mips_ram_1_p6, mips_regifile_1_r1, multiplexer_2_out, multiplexer_4_out,
       multiplexer_5_out, multiplexer_7_out, multiplexer_8_out, multiplexer_9_out, multiplexer_10_out,
       multiplexer_11_out, PC_q, shifter_1_out;

  and and_1 (and_1_out, Beq, EQ);
  not not_1 (not_1_out, EQ);
  and and_2 (and_2_out, Bne, not_1_out);
  Clock clock_1 (.out(CLK));
  Button button_1 (.out(RST));
  Register #(.width(32)) PC (.D(multiplexer_2_out), .en(PCin), .Q(PC_q), .clk(CLK), .clr(RST));
  or or_1 (PCin, JR, and_1_out, and_2_out, PCWrite);
  Multiplexer #(.width(10)) multiplexer_1 (
    .in0(PC_q[11:2]), .in1(C_q[9:0]), .out(multiplexer_1_out), .sel(IorD));  // open: en
  Multiplexer #(.width(32)) multiplexer_2 (
    .in0(multiplexer_4_out), .in1(bit_extender_1_out), .out(multiplexer_2_out), .sel(JMP));  // open: en
  // MIPS_RAM mips_ram_1: pin names not known; wires that end beside it: multiplexer_1_out, mips_ram_1_p2, MemWrite, CLK, MemRead, mips_ram_1_p6
  assign bit_extender_1_out = {{6{IR_q[25]}}, {IR_q, FUNC}};  // Bit_Extender bit_extender_1
  \多周期控制器  \u_多周期控制器_1  (
    .CLK(CLK), .Reset(RST), .op(OP), .func(FUNC), .JR(JR), .JAL(JAL), .JMP(JMP), .Bne(Bne), .Beq(Beq),
    .MemRead(MemRead), .MemWrite(MemWrite), .RegWrite(RegWrite), .PcWrite(PCWrite), .IrWrite(IRWrite),
    .RegDst(RegDes), .MemToReg(MemToReg), .AluSrcB(AluSrcB), .Shamt(Shamt), .AluSrcA(AluSrcA), .PCsrc(PcSrc),
    .IorD(IorD), .AluOp(AluOp), .out_5(\多周期控制器_1_out_5 ));
  // Probe on \多周期控制器_1_out_5 
  Register #(.width(32)) IR (.D(mips_ram_1_p6), .en(IRWrite), .Q({OP, IR_q, FUNC}), .clk(CLK), .clr(RST));
  Register #(.width(32)) DR (.D(mips_ram_1_p6), .Q(DR_q), .clk(CLK), .clr(RST));  // open: en
  assign bit_extender_2_out = {{27{1'b0}}, IR_q[10:6]};  // Bit_Extender bit_extender_2
  Multiplexer #(.width(5)) multiplexer_3 (
    .in0(IR_q[20:16]), .in1(IR_q[15:11]), .out(multiplexer_3_out), .sel(RegDes));  // open: en
  Multiplexer #(.width(32)) multiplexer_4 (
    .in0(multiplexer_11_out), .in1(A_q), .out(multiplexer_4_out), .sel(JR));  // open: en
  Multiplexer #(.width(32)) multiplexer_5 (.in0(C_q), .in1(DR_q), .out(multiplexer_5_out), .sel(MemToReg));  // open: en
  Multiplexer #(.width(5)) multiplexer_6 (
    .in0(multiplexer_3_out), .in1({5{1'b1}}), .out(multiplexer_6_out), .sel(JAL));  // open: en
  assign bit_extender_3_out = {{16{IR_q[15]}}, {IR_q[15:6], FUNC}};  // Bit_Extender bit_extender_3
  Multiplexer #(.width(32)) multiplexer_7 (
    .in0(multiplexer_5_out), .in1(PC_q), .out(multiplexer_7_out), .sel(JAL));  // open: en
  MIPS_Regifile mips_regifile_1 (
    .Din(multiplexer_7_out), .Clk(CLK), .R1(mips_regifile_1_r1), .R2(mips_ram_1_p2), .WE(RegWrite),
    .W_num(multiplexer_6_out), .R1_num(IR_q[25:21]), .R2_num(IR_q[20:16]));
  Shifter #(.width(32)) shifter_1 (.in(bit_extender_3_out), .\dist (5'b00010), .out(shifter_1_out));
  Register #(.width(32)) A (.D(mips_regifile_1_r1), .Q(A_q), .clk(CLK), .clr(RST));  // open: en
  Register #(.width(32)) B (.D(mips_ram_1_p2), .Q(B_q), .clk(CLK), .clr(RST));  // open: en
  Multiplexer #(.width(32)) multiplexer_8 (
    .in0(B_q), .in1(bit_extender_2_out), .out(multiplexer_8_out), .sel(Shamt));  // open: en
  Multiplexer #(.width(32)) multiplexer_9 (.in0(PC_q), .in1(A_q), .out(multiplexer_9_out), .sel(AluSrcA));  // open: en
  Multiplexer #(.select(2), .width(32)) multiplexer_10 (
    .in0(multiplexer_8_out), .in1(32'h4), .in2(bit_extender_3_out), .in3(shifter_1_out),
    .out(multiplexer_10_out), .sel(AluSrcB));  // open: en
  Multiplexer #(.width(32)) multiplexer_11 (
    .in0(alu_1_out_5), .in1(C_q), .out(multiplexer_11_out), .sel(PcSrc));  // open: en
  ALU alu_1 (.in_2(multiplexer_9_out), .in_3(multiplexer_10_out), .out_5(alu_1_out_5), .in_1(AluOp), .EQ(EQ));
  Register #(.width(32)) C (.D(alu_1_out_5), .Q(C_q), .clk(CLK), .clr(RST));  // open: en
endmodule

module \多周期控制器  (
  input  CLK,
  input  Reset,
  input  [5:0] op,
  input  [5:0] func,
  output [4:0] out_5,
  output JR,
  output JAL,
  output JMP,
  output Bne,
  output Beq,
  output MemRead,
  output MemWrite,
  output RegWrite,
  output PcWrite,
  output IrWrite,
  output RegDst,
  output MemToReg,
  output [1:0] AluSrcB,
  output Shamt,
  output AluSrcA,
  output PCsrc,
  output IorD,
  output [3:0] AluOp
);

  wire Beq_t, Bne_t, comparator_2_eq, comparator_3_eq, comparator_10_eq, comparator_11_lt, I, JAL_t, JMP_t,
       JR_t, LW, not_1_out, not_2_out, not_3_out, or_1_out, P, R, Shamt_t, SW;
  wire [3:0] alufunc_1_s0, aluop_1_s0, multiplexer_2_out;
  wire [4:0] multiplexer_1_out, rom_1_data, \译码器_1_n0 ;
  wire [31:24] rom_1_data_2;

  \译码器  \u_译码器_1  (
    .Rtype(R), .Itype(I), .LW(LW), .SW(SW), .BEQ(Beq_t), .BNE(Bne_t), .JR(JR_t), .JMP(JMP_t), .JAL(JAL_t),
    .Shamt(Shamt_t), .N4(\译码器_1_n0 [4]), .N3(\译码器_1_n0 [3]), .N2(\译码器_1_n0 [2]), .N1(\译码器_1_n0 [1]),
    .N0(\译码器_1_n0 [0]));
  Comparator #(.width(6)) comparator_1 (.a(op), .b({6{1'b0}}), .eq(R));  // open: gt, lt
  Multiplexer #(.width(5)) multiplexer_1 (
    .in0(rom_1_data), .in1(\译码器_1_n0 ), .out(multiplexer_1_out), .sel(P));  // open: en
  ALUOP aluop_1 (
    .op5(op[5]), .op4(op[4]), .op3(op[3]), .op2(op[2]), .op1(op[1]), .op0(op[0]), .s3(aluop_1_s0[3]),
    .s2(aluop_1_s0[2]), .s1(aluop_1_s0[1]), .s0(aluop_1_s0[0]));
  ALUFUNC alufunc_1 (
    .f5(func[5]), .f4(func[4]), .f3(func[3]), .f2(func[2]), .f1(func[1]), .f0(func[0]), .s3(alufunc_1_s0[3]),
    .s2(alufunc_1_s0[2]), .s1(alufunc_1_s0[1]), .s0(alufunc_1_s0[0]));
  Register #(.width(5)) \u_状态寄存器  (.D(multiplexer_1_out), .Q(out_5), .clk(CLK), .clr(Reset));  // open: en
  Multiplexer #(.width(4)) multiplexer_2 (
    .in0(aluop_1_s0), .in1(alufunc_1_s0), .out(multiplexer_2_out), .sel(R));  // open: en
  Comparator #(.width(5)) comparator_2 (.a(out_5), .b({5{1'b0}}), .eq(comparator_2_eq));  // open: gt, lt
  Comparator #(.width(5)) comparator_3 (.a(out_5), .b(5'b00001), .eq(comparator_3_eq));  // open: gt, lt
  ROM #(.addrWidth(5), .dataWidth(32)) rom_1 (
    .addr(out_5),
    .data({rom_1_data_2, IorD, PCsrc, AluSrcA, Shamt, AluSrcB, MemToReg, RegDst, IrWrite, PcWrite, RegWrite, MemWrite, MemRead, Beq, Bne, JMP, JAL, JR, P, rom_1_data}));  // open: sel
  Multiplexer #(.width(4)) multiplexer_3 (
    .in0(multiplexer_2_out), .in1(4'b0011), .out(AluOp), .sel(or_1_out));  // open: en
  or or_1 (or_1_out, comparator_2_eq, comparator_3_eq);
  // Probe on nothing
  Comparator #(.width(6)) comparator_4 (.a(op), .b(6'b000010), .eq(JMP_t));  // open: gt, lt
  Comparator #(.width(6)) comparator_5 (.a(op), .b(6'b000011), .eq(JAL_t));  // open: gt, lt
  Comparator #(.width(6)) comparator_6 (.a(op), .b(6'b100011), .eq(LW));  // open: gt, lt
  Comparator #(.width(6)) comparator_7 (.a(op), .b(6'b101011), .eq(SW));  // open: gt, lt
  Comparator #(.width(6)) comparator_8 (.a(op), .b(6'b000100), .eq(Beq_t));  // open: gt, lt
  Comparator #(.width(6)) comparator_9 (.a(op), .b(6'b000101), .eq(Bne_t));  // open: gt, lt
  not not_1 (not_1_out, R);
  not not_2 (not_2_out, JAL_t);
  not not_3 (not_3_out, JMP_t);
  Comparator #(.width(6)) comparator_10 (.a(func), .b(6'b001000), .eq(comparator_10_eq));  // open: gt, lt
  Comparator #(.width(6), .mode("unsigned")) comparator_11 (
    .a(func), .b(6'b000100), .lt(comparator_11_lt));  // open: gt, eq
  and and_1 (I, not_1_out, not_2_out, not_3_out);
  and and_2 (JR_t, comparator_10_eq, R);
  and and_3 (Shamt_t, R, comparator_11_lt);

  // Other names for the same wires on the sheet: 现态[4:0] = out_5

  // Notes on the sheet:
  //   contents of rom_1 (hex, n*v repeats v):
  //   4c801 c0020 280003 800804 22000 280006 801000 200008 12000 600400 600200 28000c 2000 300008 600040
  //   4100 8f
endmodule

module \译码器  (
  input  Rtype,
  input  Itype,
  input  LW,
  input  SW,
  input  BEQ,
  input  BNE,
  input  JR,
  input  JMP,
  input  JAL,
  input  Shamt,
  output N4,
  output N3,
  output N2,
  output N1,
  output N0
);

  wire and_2_out, and_3_out, and_4_out, and_5_out, and_6_out, and_7_out, and_8_out, and_9_out, and_10_out,
       and_11_out, and_12_out, and_13_out, and_14_out, and_15_out, and_16_out, and_17_out, and_18_out,
       and_19_out, and_20_out, not_1_out, not_2_out, not_3_out, not_4_out, not_5_out, not_6_out, not_7_out,
       not_8_out, not_9_out, not_10_out, not_11_out, not_12_out, not_13_out, not_14_out, not_15_out,
       not_16_out, not_17_out, not_18_out, not_19_out, not_20_out, not_21_out, not_22_out, not_23_out,
       not_24_out, not_25_out, not_26_out, not_27_out, not_28_out, not_29_out, not_30_out, not_31_out,
       not_32_out, not_33_out, not_34_out, not_35_out, not_36_out, not_37_out, not_38_out, not_39_out,
       not_40_out, not_41_out, not_42_out, not_43_out, not_44_out, not_45_out, not_46_out, not_47_out,
       not_48_out, not_49_out, not_50_out, not_51_out, not_52_out, not_53_out, not_54_out, not_55_out,
       not_56_out, not_57_out, not_58_out, not_59_out, not_60_out, not_61_out, not_62_out, not_63_out,
       not_64_out, not_65_out, not_66_out, not_67_out, not_68_out, not_69_out, not_70_out, not_71_out,
       not_72_out, not_73_out, not_74_out, not_75_out, not_76_out, not_77_out, not_78_out, not_79_out,
       not_80_out, not_81_out, not_82_out, not_83_out, not_84_out, not_85_out, not_86_out, not_87_out,
       not_88_out, not_89_out, not_90_out, not_91_out, not_92_out, not_93_out, not_94_out, not_95_out,
       not_96_out, not_97_out, not_98_out, not_99_out, not_100_out, not_101_out, not_102_out, not_103_out,
       not_104_out, not_105_out, not_106_out, not_107_out, not_108_out, not_109_out, not_110_out,
       not_111_out, not_112_out, not_113_out, not_114_out, not_115_out, not_116_out, not_117_out,
       not_118_out, not_119_out, not_120_out, not_121_out, not_122_out, not_123_out, not_124_out,
       not_125_out, not_126_out, not_127_out, not_128_out, not_129_out, not_130_out, not_131_out,
       not_132_out, not_133_out, not_134_out, not_135_out, not_136_out, not_137_out, not_138_out,
       not_139_out, not_140_out, not_141_out, not_142_out, not_143_out, not_144_out, not_145_out,
       not_146_out, not_147_out, not_148_out, not_149_out, not_150_out, not_151_out, not_152_out,
       not_153_out, not_154_out, not_155_out, not_156_out, not_157_out, not_158_out, not_159_out;

  not not_1 (not_1_out, Rtype);
  not not_2 (not_2_out, Itype);
  not not_3 (not_3_out, LW);
  not not_4 (not_4_out, SW);
  not not_5 (not_5_out, BEQ);
  not not_6 (not_6_out, BNE);
  not not_7 (not_7_out, JR);
  not not_8 (not_8_out, JMP);
  not not_9 (not_9_out, Shamt);
  not not_10 (not_10_out, Rtype);
  not not_11 (not_11_out, Itype);
  not not_12 (not_12_out, LW);
  not not_13 (not_13_out, SW);
  not not_14 (not_14_out, BEQ);
  not not_15 (not_15_out, BNE);
  not not_16 (not_16_out, JR);
  not not_17 (not_17_out, JAL);
  not not_18 (not_18_out, Shamt);
  not not_19 (not_19_out, Rtype);
  not not_20 (not_20_out, LW);
  not not_21 (not_21_out, SW);
  not not_22 (not_22_out, BEQ);
  not not_23 (not_23_out, JR);
  not not_24 (not_24_out, JMP);
  not not_25 (not_25_out, JAL);
  not not_26 (not_26_out, Shamt);
  not not_27 (not_27_out, Rtype);
  not not_28 (not_28_out, LW);
  not not_29 (not_29_out, SW);
  not not_30 (not_30_out, BNE);
  not not_31 (not_31_out, JR);
  not not_32 (not_32_out, JMP);
  not not_33 (not_33_out, JAL);
  not not_34 (not_34_out, Shamt);
  not not_35 (not_35_out, Rtype);
  not not_36 (not_36_out, LW);
  not not_37 (not_37_out, SW);
  not not_38 (not_38_out, BEQ);
  not not_39 (not_39_out, BNE);
  not not_40 (not_40_out, JAL);
  not not_41 (not_41_out, Shamt);
  not not_42 (not_42_out, Itype);
  not not_43 (not_43_out, LW);
  not not_44 (not_44_out, SW);
  not not_45 (not_45_out, BEQ);
  not not_46 (not_46_out, BNE);
  not not_47 (not_47_out, JR);
  not not_48 (not_48_out, JMP);
  not not_49 (not_49_out, JAL);
  not not_50 (not_50_out, Itype);
  not not_51 (not_51_out, LW);
  not not_52 (not_52_out, SW);
  not not_53 (not_53_out, BEQ);
  not not_54 (not_54_out, BNE);
  not not_55 (not_55_out, JMP);
  not not_56 (not_56_out, JAL);
  not not_57 (not_57_out, Shamt);
  not not_58 (not_58_out, Itype);
  not not_59 (not_59_out, LW);
  not not_60 (not_60_out, SW);
  not not_61 (not_61_out, BEQ);
  not not_62 (not_62_out, BNE);
  not not_63 (not_63_out, JR);
  not not_64 (not_64_out, JAL);
  not not_65 (not_65_out, Shamt);
  not not_66 (not_66_out, Rtype);
  not not_67 (not_67_out, LW);
  not not_68 (not_68_out, BEQ);
  not not_69 (not_69_out, BNE);
  not not_70 (not_70_out, JR);
  not not_71 (not_71_out, JMP);
  not not_72 (not_72_out, JAL);
  not not_73 (not_73_out, Shamt);
  not not_74 (not_74_out, Itype);
  not not_75 (not_75_out, LW);
  not not_76 (not_76_out, SW);
  not not_77 (not_77_out, BEQ);
  not not_78 (not_78_out, BNE);
  not not_79 (not_79_out, JR);
  not not_80 (not_80_out, JMP);
  not not_81 (not_81_out, JAL);
  not not_82 (not_82_out, Itype);
  not not_83 (not_83_out, LW);
  not not_84 (not_84_out, SW);
  not not_85 (not_85_out, BEQ);
  not not_86 (not_86_out, BNE);
  not not_87 (not_87_out, JMP);
  not not_88 (not_88_out, JAL);
  not not_89 (not_89_out, Shamt);
  not not_90 (not_90_out, Itype);
  not not_91 (not_91_out, LW);
  not not_92 (not_92_out, SW);
  not not_93 (not_93_out, BEQ);
  not not_94 (not_94_out, BNE);
  not not_95 (not_95_out, JR);
  not not_96 (not_96_out, JAL);
  not not_97 (not_97_out, Shamt);
  not not_98 (not_98_out, Rtype);
  not not_99 (not_99_out, LW);
  not not_100 (not_100_out, SW);
  not not_101 (not_101_out, BEQ);
  not not_102 (not_102_out, JR);
  not not_103 (not_103_out, JMP);
  not not_104 (not_104_out, JAL);
  not not_105 (not_105_out, Shamt);
  not not_106 (not_106_out, Rtype);
  not not_107 (not_107_out, SW);
  not not_108 (not_108_out, BEQ);
  not not_109 (not_109_out, BNE);
  not not_110 (not_110_out, JR);
  not not_111 (not_111_out, JAL);
  not not_112 (not_112_out, Shamt);
  not not_113 (not_113_out, Itype);
  not not_114 (not_114_out, LW);
  not not_115 (not_115_out, SW);
  not not_116 (not_116_out, BEQ);
  not not_117 (not_117_out, BNE);
  not not_118 (not_118_out, JMP);
  not not_119 (not_119_out, JAL);
  not not_120 (not_120_out, Shamt);
  not not_121 (not_121_out, Itype);
  not not_122 (not_122_out, LW);
  not not_123 (not_123_out, SW);
  not not_124 (not_124_out, BEQ);
  not not_125 (not_125_out, BNE);
  not not_126 (not_126_out, JR);
  not not_127 (not_127_out, JAL);
  not not_128 (not_128_out, Shamt);
  not not_129 (not_129_out, Rtype);
  not not_130 (not_130_out, LW);
  not not_131 (not_131_out, SW);
  not not_132 (not_132_out, BNE);
  not not_133 (not_133_out, JR);
  not not_134 (not_134_out, JMP);
  not not_135 (not_135_out, JAL);
  not not_136 (not_136_out, Shamt);
  not not_137 (not_137_out, Rtype);
  not not_138 (not_138_out, LW);
  not not_139 (not_139_out, BEQ);
  not not_140 (not_140_out, BNE);
  not not_141 (not_141_out, JR);
  not not_142 (not_142_out, JMP);
  not not_143 (not_143_out, JAL);
  not not_144 (not_144_out, Shamt);
  not not_145 (not_145_out, Rtype);
  not not_146 (not_146_out, LW);
  not not_147 (not_147_out, SW);
  not not_148 (not_148_out, BEQ);
  not not_149 (not_149_out, BNE);
  not not_150 (not_150_out, JAL);
  not not_151 (not_151_out, Shamt);
  not not_152 (not_152_out, Itype);
  not not_153 (not_153_out, LW);
  not not_154 (not_154_out, SW);
  not not_155 (not_155_out, BEQ);
  not not_156 (not_156_out, BNE);
  not not_157 (not_157_out, JR);
  not not_158 (not_158_out, JMP);
  not not_159 (not_159_out, JAL);
  and and_1 (N4, not_1_out, not_2_out, not_3_out, not_4_out, not_5_out, not_6_out, not_7_out, not_8_out, JAL, not_9_out);
  and and_2 (and_2_out, not_10_out, not_11_out, not_12_out, not_13_out, not_14_out, not_15_out, not_16_out, JMP, not_17_out, not_18_out);
  and and_3 (and_3_out, not_19_out, Itype, not_20_out, not_21_out, not_22_out, not_23_out, not_24_out, not_25_out, not_26_out);
  and and_4 (and_4_out, not_27_out, Itype, not_28_out, not_29_out, not_30_out, not_31_out, not_32_out, not_33_out, not_34_out);
  and and_5 (and_5_out, not_35_out, Itype, not_36_out, not_37_out, not_38_out, not_39_out, JR, not_40_out, not_41_out);
  and and_6 (and_6_out, Rtype, not_42_out, not_43_out, not_44_out, not_45_out, not_46_out, not_47_out, not_48_out, not_49_out, Shamt);
  and and_7 (and_7_out, Rtype, not_50_out, not_51_out, not_52_out, not_53_out, not_54_out, JR, not_55_out, not_56_out, not_57_out);
  and and_8 (and_8_out, not_58_out, not_59_out, not_60_out, not_61_out, not_62_out, not_63_out, JMP, not_64_out, not_65_out);
  and and_9 (and_9_out, not_66_out, Itype, not_67_out, SW, not_68_out, not_69_out, not_70_out, not_71_out, not_72_out, not_73_out);
  and and_10 (and_10_out, Rtype, not_74_out, not_75_out, not_76_out, not_77_out, not_78_out, not_79_out, not_80_out, not_81_out);
  and and_11 (and_11_out, Rtype, not_82_out, not_83_out, not_84_out, not_85_out, not_86_out, not_87_out, not_88_out, not_89_out);
  and and_12 (and_12_out, not_90_out, not_91_out, not_92_out, not_93_out, not_94_out, not_95_out, JMP, not_96_out, not_97_out);
  and and_13 (and_13_out, not_98_out, Itype, not_99_out, not_100_out, not_101_out, not_102_out, not_103_out, not_104_out, not_105_out);
  and and_14 (and_14_out, not_106_out, Itype, LW, not_107_out, not_108_out, not_109_out, not_110_out, not_111_out, not_112_out);
  and and_15 (and_15_out, Rtype, not_113_out, not_114_out, not_115_out, not_116_out, not_117_out, not_118_out, not_119_out, not_120_out);
  and and_16 (and_16_out, not_121_out, not_122_out, not_123_out, not_124_out, not_125_out, not_126_out, JMP, not_127_out, not_128_out);
  and and_17 (and_17_out, not_129_out, Itype, not_130_out, not_131_out, not_132_out, not_133_out, not_134_out, not_135_out, not_136_out);
  and and_18 (and_18_out, not_137_out, Itype, not_138_out, not_139_out, not_140_out, not_141_out, not_142_out, not_143_out, not_144_out);
  and and_19 (and_19_out, not_145_out, Itype, not_146_out, not_147_out, not_148_out, not_149_out, JR, not_150_out, not_151_out);
  and and_20 (and_20_out, Rtype, not_152_out, not_153_out, not_154_out, not_155_out, not_156_out, not_157_out, not_158_out, not_159_out);
  or or_1 (N2, and_8_out, and_9_out, and_10_out, and_11_out);
  or or_2 (N1, and_12_out, and_13_out, and_14_out, and_15_out);
  or or_3 (N0, and_16_out, and_17_out, and_18_out, and_19_out, and_20_out);
  or or_4 (N3, and_2_out, and_3_out, and_4_out, and_5_out, and_6_out, and_7_out);
endmodule
